# Fritzing sketch rpi-doorbell-proto (saved by Fritzing 0.9.4)
breadboards: 1

parts:
  MCU1 = Raspberry Pi Zero
  S1 = Pushbutton [package="[THT]"]
  R1 = Resistor [tolerance=±5% resistance=1k package=THT]
  U1 = TCM8240MD [package=tcm8240md]  # not connected

nets:
  N1: MCU1.pin_2, MCU1.pin_4, S1.Pin_1, S1.Pin_2
  N2: MCU1.pin_9, MCU1.pin_34, R1.Pin_0
  N3: MCU1.pin_11, S1.Pin_3, S1.Pin_4, R1.Pin_1
